# Fritzing sketch wiring (saved by Fritzing 0.9.2b)

parts:
  Part1 = Arduino Uno (Rev3)
  J1 = Basic Servo
  J2 = Basic Servo

nets:
  N1: Part1.D10_PWM/SS, J2.pulse
  N2: Part1.D11_PWM/MOSI, J1.pulse
  VCC: Part1.5V, J1.vcc, J2.vcc
  GND: Part1.GND, J1.gnd, J2.gnd
